# Fritzing sketch LED_Group_Perfboard (saved by Fritzing 0.9.2b)
perfboards: 1

parts:
  U1 = Packages: [package=dil28-3]
  U2 = Packages: [package=dil28-3]
  R1 = Resistor [tolerance=±5% resistance=1.91k package=THT]
  R2 = Resistor [tolerance=±5% resistance=1.91k package=THT]
  LED10 = LED - 5mm [color="Infrared (940nm)" package="5 mm [THT]"]
  C1 = Ceramic Capacitor [capacitance=0.1µF package="100 mil [THT, multilayer]"]
  C2 = Ceramic Capacitor [capacitance=0.1µF package="100 mil [THT, multilayer]"]
  J1 = female pin header, 4 pins [form="♀ (female)"]
  J11 = female pin header, 5 pins [form="♀ (female)"]
  J12 = female pin header, 5 pins [form="♀ (female)"]
  J2 = female pin header, 4 pins [form="♀ (female)"]
  J3 = female pin header, 4 pins [form="♀ (female)"]
  J5 = female pin header, 4 pins [form="♀ (female)"]
  J6 = female pin header, 4 pins [form="♀ (female)"]
  J7 = female pin header, 4 pins [form="♀ (female)"]
  J8 = female pin header, 4 pins [form="♀ (female)"]
  J9 = female pin header, 4 pins [form="♀ (female)"]
  R3 = Resistor [tolerance=±5% resistance=75 package=THT]
  J10 = female pin header, 5 pins [form="♀ (female)"]
  IR1 = TSOP312.., 314.. [package=THT]
  J4 = female pin header, 4 pins [form="♀ (female)"]
  C3 = Ceramic Capacitor [capacitance=0.1µF package="200 mil [THT, multilayer]"]

nets:
  N1: U1.OUT1, J1.pin3
  N2: U1.OUT2, J1.pin4
  N3: U1.OUT3, J2.pin2
  N4: U1.OUT4, J2.pin3
  N5: U1.OUT5, J2.pin4
  N6: U1.OUT6, J3.pin2
  N7: U1.OUT7, J3.pin3
  N8: U1.OUT8, J3.pin4
  N9: U1.OUT9, J4.pin2
  N10: U1.OUT10, J4.pin3
  N11: U1.OUT11, J4.pin4
  N12: U1.OUT12, J5.pin2
  N13: U1.OUT13, J5.pin3
  N14: U1.OUT14, J5.pin4
  N15: U1.SOUT, U2.SIN
  N16: U1.GSCLK, J11.pin5
  5V: U1.DCPRG, U1.VCC, U2.DCPRG, U2.VCC, LED10.anode, C1.1, C2.1, J1.pin1, J2.pin1, J3.pin1, J5.pin1, J6.pin1, J7.pin1, J8.pin1, J9.pin1, R3.Pin_0, J10.pin1, J4.pin1, C3.1
  N17: U1.IREF, R1.Pin_1
  GND: U1.GND, U2.GND, R1.Pin_0, R2.Pin_0, C1.0, C2.0, J10.pin5, IR1.GND, C3.0
  N18: U1.BLANK, J11.pin1
  N19: U1.XLAT, J11.pin4
  N20: U1.SCLK, J11.pin2
  N21: U1.SIN, J11.pin3
  N22: U1.OUT0, J1.pin2
  N23: U2.OUT1, J6.pin3
  N24: U2.OUT2, J6.pin4
  N25: U2.OUT3, J7.pin2
  N26: U2.OUT4, J7.pin3
  N27: U2.OUT5, J7.pin4
  N28: U2.OUT6, J8.pin2
  N29: U2.OUT7, J8.pin3
  N30: U2.OUT8, J8.pin4
  N31: U2.OUT9, J9.pin2
  N32: U2.OUT10, J9.pin3
  N33: U2.OUT11, J9.pin4
  N34: U2.SOUT, J12.pin3
  N35: U2.GSCLK, J12.pin5
  N36: U2.IREF, R2.Pin_1
  N37: U2.BLANK, J12.pin1
  N38: U2.XLAT, J12.pin4
  N39: U2.SCLK, J12.pin2
  N40: U2.OUT0, J6.pin2
  N41: LED10.cathode, J10.pin2
  N42: R3.Pin_1, J10.pin3, IR1.Vs
  N43: J10.pin4, IR1.Data

notes:
  Input
  Output
  PWR&IR
  LED1
  LED2
  LED3
  LED5
  LED4
  LED6
  LED7
  LED8
  LED9
